# Fritzing sketch Untitled Sketch 2 (saved by Fritzing 0.9.3b)
breadboards: 1

parts:
  Part1 = Arduino Uno (Rev3)
  Q1 = NPN-Transistor [package="TO92 [THT]"]
  Q2 = NPN-Transistor [package="TO92 [THT]"]
  Q3 = NPN-Transistor [package="TO92 [THT]"]
  J1 = shrouded pin header, 10 pins [form="♂ (shrouded male)"]
  LED1 = RGB LED (com. cathode, rgb) [package="5 mm [THT]"]
  Power_plug1 = Power plug

nets:
  N1: Part1.D9_PWM, Q1.B
  N2: Part1.D10_PWM/SS, J1.pin9
  N3: Part1.D11_PWM/MOSI, J1.pin3
  N4: Part1.D12/MISO, J1.pin4
  N5: Part1.D13/SCK, J1.pin2
  N6: Part1.D5_PWM, Q3.B
  N7: Part1.D6_PWM, Q2.B
  N8: Part1.GND, J1.pin1
  N9: Part1.VIN, J1.pin8
  N10: Q1.E, Q2.E, Q3.E, Power_plug1.GND
  N11: Q1.C, LED1.blue_anode
  N12: Q2.C, LED1.green_anode
  N13: Q3.C, LED1.red_anode
  N14: LED1.common_cathode, Power_plug1.VCC
